// Logisim project ProjetoALU.circ as structural Verilog: 7 circuits, main circuit main
module main (
  input  [7:0] A,
  input  [7:0] B,
  input  [3:0] Seletor,
  output [7:0] S
);

  wire [7:0] and_1_out, multiplier_1_out, nand_1_out, nor_1_out, not_1_out, or_1_out, shifter_1_out,
       shifter_2_out, somador_8bits_1_s, subtrator_8bits_1_s, xnor_1_out, xor_1_out;

  Multiplier multiplier_1 (.a(A), .b(B), .out(multiplier_1_out));  // open: cin, cout
  Shifter #(.shift("lr")) shifter_1 (.in(A), .\dist (3'b010), .out(shifter_1_out));
  assign nand_1_out = ~(A & B);  // NAND_Gate nand_1, 8 bits wide
  assign not_1_out = ~A;  // NOT_Gate not_1, 8 bits wide
  assign or_1_out = A | B;  // OR_Gate or_1, 8 bits wide
  assign xnor_1_out = ~(A ^ B);  // XNOR_Gate xnor_1, 8 bits wide
  Shifter shifter_2 (.in(A), .\dist (3'b100), .out(shifter_2_out));
  assign xor_1_out = A ^ B;  // XOR_Gate xor_1, 8 bits wide
  assign and_1_out = A & B;  // AND_Gate and_1, 8 bits wide
  assign nor_1_out = ~(A | B);  // NOR_Gate nor_1, 8 bits wide
  Subtrator_8bits subtrator_8bits_1 (.S(subtrator_8bits_1_s), .A(A), .B(B));
  Somador_8bits somador_8bits_1 (.S(somador_8bits_1_s), .B(B), .A(A));
  Multiplexer #(.select(4), .width(8), .enable("false")) multiplexer_1 (
    .in0({8{1'b0}}), .in1(subtrator_8bits_1_s), .in2(multiplier_1_out), .in3({8{1'b0}}), .in4(shifter_1_out),
    .in5(nand_1_out), .in6({8{1'b0}}), .in7(somador_8bits_1_s), .in8(not_1_out), .in9(or_1_out),
    .in10(xnor_1_out), .in11(shifter_2_out), .in12(xor_1_out), .in13({8{1'b0}}), .in14(and_1_out),
    .in15(nor_1_out), .out(S), .sel(Seletor));
endmodule

module MeioSomador (
  input  A,
  input  B,
  output S,
  output Cout
);

  xor xor_1 (S, A, B);
  and and_1 (Cout, A, B);
endmodule

module SomadorCompleto (
  input  A,
  input  B,
  input  carryIN,
  output SOMA,
  output carryOUT
);

  wire meiosomador_1_cout, meiosomador_1_s, meiosomador_2_cout;

  MeioSomador meiosomador_1 (.Cout(meiosomador_1_cout), .B(B), .S(meiosomador_1_s), .A(A));
  MeioSomador meiosomador_2 (.Cout(meiosomador_2_cout), .B(carryIN), .S(SOMA), .A(meiosomador_1_s));
  or or_1 (carryOUT, meiosomador_2_cout, meiosomador_1_cout);
endmodule

module Somador_8bits (
  input  [7:0] A,
  input  [7:0] B,
  output [7:0] S
);

  wire somadorcompleto_1_carryout, somadorcompleto_2_carryout, somadorcompleto_3_carryout,
       somadorcompleto_4_carryout, somadorcompleto_5_carryout, somadorcompleto_6_carryout,
       somadorcompleto_7_carryout, somadorcompleto_8_carryout;

  SomadorCompleto somadorcompleto_1 (
    .SOMA(S[7]), .A(A[7]), .carryOUT(somadorcompleto_1_carryout), .carryIN(somadorcompleto_2_carryout),
    .B(B[7]));
  SomadorCompleto somadorcompleto_2 (
    .SOMA(S[6]), .A(A[6]), .carryOUT(somadorcompleto_2_carryout), .carryIN(somadorcompleto_3_carryout),
    .B(B[6]));
  SomadorCompleto somadorcompleto_3 (
    .SOMA(S[5]), .A(A[5]), .carryOUT(somadorcompleto_3_carryout), .carryIN(somadorcompleto_4_carryout),
    .B(B[5]));
  SomadorCompleto somadorcompleto_4 (
    .SOMA(S[4]), .A(A[4]), .carryOUT(somadorcompleto_4_carryout), .carryIN(somadorcompleto_5_carryout),
    .B(B[4]));
  SomadorCompleto somadorcompleto_5 (
    .SOMA(S[3]), .A(A[3]), .carryOUT(somadorcompleto_5_carryout), .carryIN(somadorcompleto_6_carryout),
    .B(B[3]));
  SomadorCompleto somadorcompleto_6 (
    .SOMA(S[2]), .A(A[2]), .carryOUT(somadorcompleto_6_carryout), .carryIN(somadorcompleto_7_carryout),
    .B(B[2]));
  SomadorCompleto somadorcompleto_7 (
    .SOMA(S[1]), .A(A[1]), .carryOUT(somadorcompleto_7_carryout), .carryIN(somadorcompleto_8_carryout),
    .B(B[1]));
  SomadorCompleto somadorcompleto_8 (
    .SOMA(S[0]), .A(A[0]), .carryOUT(somadorcompleto_8_carryout), .carryIN(1'b0), .B(B[0]));
  // also tied to GND on the sheet: somadorcompleto_1_carryout
endmodule

module MeioSubtrator (
  input  A,
  input  B,
  output S,
  output Tout
);

  wire not_1_out;

  not not_1 (not_1_out, A);
  xor xor_1 (S, A, B);
  and and_1 (Tout, B, not_1_out);
endmodule

module SubtratorCompleto (
  input  A,
  input  B,
  input  BORROW_IN,
  output S,
  output BORROW_OUT
);

  wire meiosubtrator_1_s, meiosubtrator_1_tout, meiosubtrator_2_tout;

  MeioSubtrator meiosubtrator_1 (.S(meiosubtrator_1_s), .B(B), .Tout(meiosubtrator_1_tout), .A(A));
  MeioSubtrator meiosubtrator_2 (.S(S), .B(BORROW_IN), .Tout(meiosubtrator_2_tout), .A(meiosubtrator_1_s));
  or or_1 (BORROW_OUT, meiosubtrator_2_tout, meiosubtrator_1_tout);
endmodule

module Subtrator_8bits (
  input  [7:0] A,
  input  [7:0] B,
  output [7:0] S
);

  wire subtratorcompleto_1_borrow_out, subtratorcompleto_2_borrow_out, subtratorcompleto_3_borrow_out,
       subtratorcompleto_4_borrow_out, subtratorcompleto_5_borrow_out, subtratorcompleto_6_borrow_out,
       subtratorcompleto_7_borrow_out, subtratorcompleto_8_borrow_out;

  SubtratorCompleto subtratorcompleto_1 (
    .S(S[7]), .A(A[7]), .BORROW_OUT(subtratorcompleto_1_borrow_out),
    .BORROW_IN(subtratorcompleto_2_borrow_out), .B(B[7]));
  SubtratorCompleto subtratorcompleto_2 (
    .S(S[6]), .A(A[6]), .BORROW_OUT(subtratorcompleto_2_borrow_out),
    .BORROW_IN(subtratorcompleto_3_borrow_out), .B(B[6]));
  SubtratorCompleto subtratorcompleto_3 (
    .S(S[5]), .A(A[5]), .BORROW_OUT(subtratorcompleto_3_borrow_out),
    .BORROW_IN(subtratorcompleto_4_borrow_out), .B(B[5]));
  SubtratorCompleto subtratorcompleto_4 (
    .S(S[4]), .A(A[4]), .BORROW_OUT(subtratorcompleto_4_borrow_out),
    .BORROW_IN(subtratorcompleto_5_borrow_out), .B(B[4]));
  SubtratorCompleto subtratorcompleto_5 (
    .S(S[3]), .A(A[3]), .BORROW_OUT(subtratorcompleto_5_borrow_out),
    .BORROW_IN(subtratorcompleto_6_borrow_out), .B(B[3]));
  SubtratorCompleto subtratorcompleto_6 (
    .S(S[2]), .A(A[2]), .BORROW_OUT(subtratorcompleto_6_borrow_out),
    .BORROW_IN(subtratorcompleto_7_borrow_out), .B(B[2]));
  SubtratorCompleto subtratorcompleto_7 (
    .S(S[1]), .A(A[1]), .BORROW_OUT(subtratorcompleto_7_borrow_out),
    .BORROW_IN(subtratorcompleto_8_borrow_out), .B(B[1]));
  SubtratorCompleto subtratorcompleto_8 (
    .S(S[0]), .A(A[0]), .BORROW_OUT(subtratorcompleto_8_borrow_out), .BORROW_IN(1'b0), .B(B[0]));
  // also tied to GND on the sheet: subtratorcompleto_1_borrow_out
endmodule
