// Logisim project Aula01.circ as structural Verilog
module meioSomador (
  input  A,
  input  B,
  output S,
  output Cout
);

  xor xor_1 (S, A, B);
  and and_1 (Cout, A, B);
endmodule

module SomadorCompleto (
  input  A,
  input  B,
  input  CARRYIN,
  output SOMA,
  output CARRYOUT
);

  wire meiosomador_1_cout, meiosomador_1_s, meiosomador_2_cout;

  meioSomador meiosomador_1 (.Cout(meiosomador_1_cout), .S(meiosomador_1_s), .A(A), .B(B));
  meioSomador meiosomador_2 (.Cout(meiosomador_2_cout), .S(SOMA), .A(meiosomador_1_s), .B(CARRYIN));
  or or_1 (CARRYOUT, meiosomador_2_cout, meiosomador_1_cout);
endmodule

module Somador_4bits (
  input  [3:0] A,
  input  [3:0] B,
  output [3:0] S
);

  wire somadorcompleto_1_carryout, somadorcompleto_2_carryout, somadorcompleto_3_carryout,
       somadorcompleto_4_carryout;

  SomadorCompleto somadorcompleto_1 (
    .CARRYOUT(somadorcompleto_1_carryout), .SOMA(S[3]), .B(B[3]), .A(A[3]),
    .CARRYIN(somadorcompleto_2_carryout));
  SomadorCompleto somadorcompleto_2 (
    .CARRYOUT(somadorcompleto_2_carryout), .SOMA(S[2]), .B(B[2]), .A(A[2]),
    .CARRYIN(somadorcompleto_3_carryout));
  SomadorCompleto somadorcompleto_3 (
    .CARRYOUT(somadorcompleto_3_carryout), .SOMA(S[1]), .B(B[1]), .A(A[1]),
    .CARRYIN(somadorcompleto_4_carryout));
  SomadorCompleto somadorcompleto_4 (
    .CARRYOUT(somadorcompleto_4_carryout), .SOMA(S[0]), .B(B[0]), .A(A[0]), .CARRYIN(1'b0));
  // also tied to GND on the sheet: somadorcompleto_1_carryout
endmodule

module meioSubtrator (
  input  A,
  input  B,
  output S,
  output Tout
);

  wire not_1_out;

  not not_1 (not_1_out, A);
  xor xor_1 (S, A, B);
  and and_1 (Tout, B, not_1_out);
endmodule

module SubtratorCompleto (
  input  A,
  input  B,
  input  BORROW_IN,
  output S,
  output BORROW_OUT
);

  wire meiosubtrator_1_s, meiosubtrator_1_tout, meiosubtrator_2_tout;

  meioSubtrator meiosubtrator_1 (.Tout(meiosubtrator_1_tout), .B(B), .S(meiosubtrator_1_s), .A(A));
  meioSubtrator meiosubtrator_2 (.Tout(meiosubtrator_2_tout), .B(BORROW_IN), .S(S), .A(meiosubtrator_1_s));
  or or_1 (BORROW_OUT, meiosubtrator_2_tout, meiosubtrator_1_tout);
endmodule

module Subtrator_4bits (
  input  [3:0] A,
  input  [3:0] B,
  output [3:0] S
);

  wire subtratorcompleto_1_borrow_out, subtratorcompleto_2_borrow_out, subtratorcompleto_3_borrow_out,
       subtratorcompleto_4_borrow_out;

  SubtratorCompleto subtratorcompleto_1 (
    .A(A[3]), .BORROW_IN(subtratorcompleto_2_borrow_out), .B(B[3]), .S(S[3]),
    .BORROW_OUT(subtratorcompleto_1_borrow_out));
  SubtratorCompleto subtratorcompleto_2 (
    .A(A[2]), .BORROW_IN(subtratorcompleto_3_borrow_out), .B(B[2]), .S(S[2]),
    .BORROW_OUT(subtratorcompleto_2_borrow_out));
  SubtratorCompleto subtratorcompleto_3 (
    .A(A[1]), .BORROW_IN(subtratorcompleto_4_borrow_out), .B(B[1]), .S(S[1]),
    .BORROW_OUT(subtratorcompleto_3_borrow_out));
  SubtratorCompleto subtratorcompleto_4 (
    .A(A[0]), .BORROW_IN(1'b0), .B(B[0]), .S(S[0]), .BORROW_OUT(subtratorcompleto_4_borrow_out));
  // also tied to GND on the sheet: subtratorcompleto_1_borrow_out
endmodule

module Relatorio01_ex01 (
  input  A,
  input  S1,
  input  B,
  output S,
  output CTout
);

  wire demultiplexer_1_out0, demultiplexer_1_out1, demultiplexer_2_out0, demultiplexer_2_out1,
       meiosomador_1_cout, meiosomador_1_s, meiosubtrator_1_s, meiosubtrator_1_tout;

  Demultiplexer #(.enable("false")) demultiplexer_1 (
    .out0(demultiplexer_1_out0), .out1(demultiplexer_1_out1), .in(A), .sel(S1));
  Demultiplexer #(.enable("false")) demultiplexer_2 (
    .out0(demultiplexer_2_out0), .out1(demultiplexer_2_out1), .in(B), .sel(S1));
  meioSomador meiosomador_1 (
    .Cout(meiosomador_1_cout), .S(meiosomador_1_s), .A(demultiplexer_1_out0), .B(demultiplexer_2_out0));
  meioSubtrator meiosubtrator_1 (
    .Tout(meiosubtrator_1_tout), .B(demultiplexer_2_out1), .S(meiosubtrator_1_s), .A(demultiplexer_1_out1));
  Multiplexer #(.enable("false")) multiplexer_1 (.in0(meiosomador_1_s), .in1(meiosubtrator_1_s), .out(S), .sel(S1));
  Multiplexer #(.enable("false")) multiplexer_2 (
    .in0(meiosomador_1_cout), .in1(meiosubtrator_1_tout), .out(CTout), .sel(S1));
endmodule

module Relatorio01_ex02 (
  input  [3:0] A,
  input  in_2,
  input  [3:0] B,
  output [3:0] out_4
);

  wire [3:0] demultiplexer_1_out0, demultiplexer_1_out1, demultiplexer_2_out0, demultiplexer_2_out1,
       somador_4bits_1_s, subtrator_4bits_1_s;

  Demultiplexer #(.width(4), .enable("false")) demultiplexer_1 (
    .out0(demultiplexer_1_out0), .out1(demultiplexer_1_out1), .in(A), .sel(in_2));
  Demultiplexer #(.width(4), .enable("false")) demultiplexer_2 (
    .out0(demultiplexer_2_out0), .out1(demultiplexer_2_out1), .in(B), .sel(in_2));
  Somador_4bits somador_4bits_1 (.A(demultiplexer_1_out0), .B(demultiplexer_2_out0), .S(somador_4bits_1_s));
  Subtrator_4bits subtrator_4bits_1 (.A(demultiplexer_1_out1), .B(demultiplexer_2_out1), .S(subtrator_4bits_1_s));
  Multiplexer #(.width(4), .enable("false")) multiplexer_1 (
    .in0(somador_4bits_1_s), .in1(subtrator_4bits_1_s), .out(out_4), .sel(in_2));
endmodule
