// Logisim project Aula02.circ as structural Verilog
module meioSomador (
  input  A,
  input  B,
  output S,
  output Cout
);

  xor xor_1 (S, A, B);
  and and_1 (Cout, A, B);
endmodule

module SomadorCompleto (
  input  A,
  input  B,
  input  CARRYIN,
  output SOMA,
  output CARRYOUT
);

  wire meiosomador_1_cout, meiosomador_1_s, meiosomador_2_cout;

  meioSomador meiosomador_1 (.S(meiosomador_1_s), .B(B), .A(A), .Cout(meiosomador_1_cout));
  meioSomador meiosomador_2 (.S(SOMA), .B(CARRYIN), .A(meiosomador_1_s), .Cout(meiosomador_2_cout));
  or or_1 (CARRYOUT, meiosomador_2_cout, meiosomador_1_cout);
endmodule

module Somador_4bits (
  input  [3:0] A,
  input  [3:0] B,
  output [3:0] S
);

  wire somadorcompleto_1_carryout, somadorcompleto_2_carryout, somadorcompleto_3_carryout,
       somadorcompleto_4_carryout;

  SomadorCompleto somadorcompleto_1 (
    .CARRYOUT(somadorcompleto_1_carryout), .B(B[3]), .CARRYIN(somadorcompleto_2_carryout), .A(A[3]),
    .SOMA(S[3]));
  SomadorCompleto somadorcompleto_2 (
    .CARRYOUT(somadorcompleto_2_carryout), .B(B[2]), .CARRYIN(somadorcompleto_3_carryout), .A(A[2]),
    .SOMA(S[2]));
  SomadorCompleto somadorcompleto_3 (
    .CARRYOUT(somadorcompleto_3_carryout), .B(B[1]), .CARRYIN(somadorcompleto_4_carryout), .A(A[1]),
    .SOMA(S[1]));
  SomadorCompleto somadorcompleto_4 (
    .CARRYOUT(somadorcompleto_4_carryout), .B(B[0]), .CARRYIN(1'b0), .A(A[0]), .SOMA(S[0]));
  // also tied to GND on the sheet: somadorcompleto_1_carryout
endmodule

module meioSubtrator (
  input  A,
  input  B,
  output S,
  output Tout
);

  wire not_1_out;

  not not_1 (not_1_out, A);
  xor xor_1 (S, A, B);
  and and_1 (Tout, B, not_1_out);
endmodule

module SubtratorCompleto (
  input  A,
  input  B,
  input  BORROW_IN,
  output S,
  output BORROW_OUT
);

  wire meiosubtrator_1_s, meiosubtrator_1_tout, meiosubtrator_2_tout;

  meioSubtrator meiosubtrator_1 (.Tout(meiosubtrator_1_tout), .S(meiosubtrator_1_s), .B(B), .A(A));
  meioSubtrator meiosubtrator_2 (.Tout(meiosubtrator_2_tout), .S(S), .B(BORROW_IN), .A(meiosubtrator_1_s));
  or or_1 (BORROW_OUT, meiosubtrator_2_tout, meiosubtrator_1_tout);
endmodule

module Subtrator_4bits (
  input  [3:0] A,
  input  [3:0] B,
  output [3:0] S
);

  wire subtratorcompleto_1_borrow_out, subtratorcompleto_2_borrow_out, subtratorcompleto_3_borrow_out,
       subtratorcompleto_4_borrow_out;

  SubtratorCompleto subtratorcompleto_1 (
    .BORROW_OUT(subtratorcompleto_1_borrow_out), .B(B[3]), .BORROW_IN(subtratorcompleto_2_borrow_out),
    .A(A[3]), .S(S[3]));
  SubtratorCompleto subtratorcompleto_2 (
    .BORROW_OUT(subtratorcompleto_2_borrow_out), .B(B[2]), .BORROW_IN(subtratorcompleto_3_borrow_out),
    .A(A[2]), .S(S[2]));
  SubtratorCompleto subtratorcompleto_3 (
    .BORROW_OUT(subtratorcompleto_3_borrow_out), .B(B[1]), .BORROW_IN(subtratorcompleto_4_borrow_out),
    .A(A[1]), .S(S[1]));
  SubtratorCompleto subtratorcompleto_4 (
    .BORROW_OUT(subtratorcompleto_4_borrow_out), .B(B[0]), .BORROW_IN(1'b0), .A(A[0]), .S(S[0]));
  // also tied to GND on the sheet: subtratorcompleto_1_borrow_out
endmodule

module SomadorSinalizado (
  input  [3:0] A,
  input  [3:0] B,
  input  Cin,
  output Cout,
  output [3:0] S
);

  wire multiplexer_1_out, multiplexer_2_out, multiplexer_3_out, multiplexer_4_out, not_1_out, not_2_out,
       not_3_out, not_4_out, somadorcompleto_2_carryout, somadorcompleto_3_carryout,
       somadorcompleto_4_carryout;

  not not_1 (not_1_out, B[3]);
  Multiplexer #(.enable("false")) multiplexer_1 (.in0(B[3]), .in1(not_1_out), .out(multiplexer_1_out), .sel(Cin));
  SomadorCompleto somadorcompleto_1 (
    .CARRYOUT(Cout), .B(multiplexer_1_out), .CARRYIN(somadorcompleto_2_carryout), .A(A[3]), .SOMA(S[0]));
  not not_2 (not_2_out, B[2]);
  Multiplexer #(.enable("false")) multiplexer_2 (.in0(B[2]), .in1(not_2_out), .out(multiplexer_2_out), .sel(Cin));
  SomadorCompleto somadorcompleto_2 (
    .CARRYOUT(somadorcompleto_2_carryout), .B(multiplexer_2_out), .CARRYIN(somadorcompleto_3_carryout),
    .A(A[2]), .SOMA(S[1]));
  not not_3 (not_3_out, B[1]);
  Multiplexer #(.enable("false")) multiplexer_3 (.in0(B[1]), .in1(not_3_out), .out(multiplexer_3_out), .sel(Cin));
  SomadorCompleto somadorcompleto_3 (
    .CARRYOUT(somadorcompleto_3_carryout), .B(multiplexer_3_out), .CARRYIN(somadorcompleto_4_carryout),
    .A(A[1]), .SOMA(S[2]));
  not not_4 (not_4_out, B[0]);
  Multiplexer #(.enable("false")) multiplexer_4 (.in0(B[0]), .in1(not_4_out), .out(multiplexer_4_out), .sel(Cin));
  SomadorCompleto somadorcompleto_4 (
    .CARRYOUT(somadorcompleto_4_carryout), .B(multiplexer_4_out), .CARRYIN(Cin), .A(A[0]), .SOMA(S[3]));
endmodule

module Multiplicador (
  input  A0,
  input  A1,
  input  B1,
  input  B0,
  output P3,
  output P2,
  output P1,
  output P0
);

  wire and_1_out, and_2_out, and_3_out, meiosomador_2_cout;

  and and_1 (and_1_out, A1, B1);
  meioSomador meiosomador_1 (.S(P2), .B(and_1_out), .A(meiosomador_2_cout), .Cout(P3));
  and and_2 (and_2_out, A1, B0);
  and and_3 (and_3_out, A0, B1);
  meioSomador meiosomador_2 (.S(P1), .B(and_2_out), .A(and_3_out), .Cout(meiosomador_2_cout));
  and and_4 (P0, A0, B0);
endmodule

module Registrador (
  input  [3:0] D,
  input  Clock,
  input  Carga,
  input  Clear,
  output [3:0] Q
);

  wire multiplexer_1_out, multiplexer_2_out, multiplexer_3_out, multiplexer_4_out;

  D_Flip_Flop d_ff_1 (.D(multiplexer_1_out), .clk(Clock), .Q(Q[3]), .reset(Clear));  // open: Qn, preset
  Multiplexer #(.enable("false")) multiplexer_1 (.in0(Q[3]), .in1(D[3]), .out(multiplexer_1_out), .sel(Carga));
  D_Flip_Flop d_ff_2 (.D(multiplexer_2_out), .clk(Clock), .Q(Q[2]), .reset(Clear));  // open: Qn, preset
  Multiplexer #(.enable("false")) multiplexer_2 (.in0(Q[2]), .in1(D[2]), .out(multiplexer_2_out), .sel(Carga));
  D_Flip_Flop d_ff_3 (.D(multiplexer_3_out), .clk(Clock), .Q(Q[1]), .reset(Clear));  // open: Qn, preset
  Multiplexer #(.enable("false")) multiplexer_3 (.in0(Q[1]), .in1(D[1]), .out(multiplexer_3_out), .sel(Carga));
  D_Flip_Flop d_ff_4 (.D(multiplexer_4_out), .clk(Clock), .Q(Q[0]), .reset(Clear));  // open: Qn, preset
  Multiplexer #(.enable("false")) multiplexer_4 (.in0(Q[0]), .in1(D[0]), .out(multiplexer_4_out), .sel(Carga));
endmodule
